// Logisim project fpadder.circ as structural Verilog: 1 circuit, main circuit main
module main (
  input  in_1,
  input  [15:0] in_2,
  input  [15:0] in_3,
  input  [15:0] in_4,
  input  in_5,
  input  in_6,
  input  [15:0] in_7,
  input  in_8,
  input  [3:0] in_9,
  input  [3:0] in_10,
  input  in_11,
  input  in_12,
  input  in_13,
  input  in_14,
  input  in_15,
  output out_16,
  output [3:0] out_17,
  output [3:0] out_18,
  output out_19,
  output [15:0] out_20,
  output [3:0] out_21
);

  wire and_1_out, comparator_1_lt, multiplexer_6_out, multiplexer_9_out, multiplexer_11_out, not_1_out,
       not_2_out, subtractor_1_bout, xor_1_out;
  wire [3:0] adder_5_out, bit_extender_1_out, bit_extender_2_out, bitfinder_1_index, multiplexer_1_out,
       multiplexer_4_out, subtractor_1_out, subtractor_3_out;
  wire [15:0] adder_2_out, adder_3_out, adder_4_out, multiplexer_2_out, multiplexer_3_out, multiplexer_5_out,
       multiplexer_8_out, multiplexer_10_out, or_1_out, or_2_out, or_3_out, shifter_1_out, shifter_2_out,
       shifter_3_out, shifter_4_out, shifter_5_out, shifter_6_out, xor_3_out, xor_4_out;

  Subtractor #(.width(4)) subtractor_1 (
    .a(in_9), .b(in_10), .out(subtractor_1_out), .bin(in_8), .bout(subtractor_1_bout));
  xor xor_1 (xor_1_out, in_14, in_15);
  Shifter #(.width(16), .shift("lr")) shifter_1 (.in(in_3), .\dist (4'b0001), .out(shifter_1_out));
  Shifter #(.width(16), .shift("lr")) shifter_2 (.in(in_4), .\dist (4'b0001), .out(shifter_2_out));
  assign out_17 = subtractor_1_out ^ 4'b1111;  // XOR_Gate xor_2, 4 bits wide
  Multiplexer #(.width(4)) multiplexer_1 (
    .in0(in_9), .in1(in_10), .out(multiplexer_1_out), .sel(subtractor_1_bout), .en(in_13));
  assign or_1_out = shifter_1_out | in_2;  // OR_Gate or_1, 16 bits wide
  assign or_2_out = shifter_2_out | in_7;  // OR_Gate or_2, 16 bits wide
  Adder #(.width(4)) adder_1 (.a(out_17), .b(4'b0001), .out(out_18));  // open: cin, cout
  Multiplexer #(.width(16)) multiplexer_2 (
    .in0(or_1_out), .in1(or_2_out), .out(multiplexer_2_out), .sel(not_2_out), .en(in_13));
  not not_1 (not_1_out, not_2_out);
  not not_2 (not_2_out, subtractor_1_bout);
  Multiplexer #(.width(16)) multiplexer_3 (
    .in0(or_1_out), .in1(or_2_out), .out(multiplexer_3_out), .sel(not_1_out), .en(in_13));
  Multiplexer #(.width(4)) multiplexer_4 (
    .in0(subtractor_1_out), .in1(out_18), .out(multiplexer_4_out), .sel(subtractor_1_bout), .en(in_13));
  Shifter #(.width(16), .shift("lr")) shifter_3 (
    .in(multiplexer_2_out), .\dist (multiplexer_4_out), .out(shifter_3_out));
  assign xor_3_out = shifter_3_out ^ {16{1'b1}};  // XOR_Gate xor_3, 16 bits wide
  Adder #(.width(16)) adder_2 (.a(xor_3_out), .b(16'h1), .out(adder_2_out));  // open: cin, cout
  Multiplexer #(.width(16)) multiplexer_5 (
    .in0(shifter_3_out), .in1(adder_2_out), .out(multiplexer_5_out), .sel(xor_1_out), .en(in_13));
  Shifter #(.width(16), .shift("lr")) shifter_4 (.in(multiplexer_3_out), .\dist (4'b0001), .out(shifter_4_out));
  Shifter #(.width(16), .shift("lr")) shifter_5 (.in(multiplexer_5_out), .\dist (4'b0001), .out(shifter_5_out));
  Adder #(.width(16)) adder_3 (
    .a(multiplexer_3_out), .b(multiplexer_5_out), .out(adder_3_out), .cin(in_1), .cout(out_16));
  Comparator #(.width(16)) comparator_1 (.a(shifter_4_out), .b(shifter_5_out), .lt(comparator_1_lt));  // open: gt, eq
  Multiplexer multiplexer_6 (.in0(in_14), .in1(in_15), .out(multiplexer_6_out), .sel(comparator_1_lt), .en(in_13));
  assign xor_4_out = adder_3_out ^ {16{1'b1}};  // XOR_Gate xor_4, 16 bits wide
  Adder #(.width(16)) adder_4 (.a(xor_4_out), .b(16'h1), .out(adder_4_out));  // open: cin, cout
  and and_1 (and_1_out, out_16, xor_1_out);
  Multiplexer multiplexer_7 (.in0(in_14), .in1(multiplexer_6_out), .out(out_19), .sel(xor_1_out), .en(in_13));
  Multiplexer #(.width(16)) multiplexer_8 (
    .in0(adder_3_out), .in1(adder_4_out), .out(multiplexer_8_out), .sel(and_1_out), .en(in_13));
  Multiplexer multiplexer_9 (.in0(in_5), .in1(in_6), .out(multiplexer_9_out), .sel(out_16), .en(in_13));
  assign bit_extender_1_out = {{3{1'b0}}, multiplexer_9_out};  // Bit_Extender bit_extender_1
  Shifter #(.width(16), .shift("lr")) shifter_6 (
    .in(multiplexer_8_out), .\dist (bit_extender_1_out), .out(shifter_6_out));
  Multiplexer #(.width(16)) multiplexer_10 (
    .in0({16{1'b0}}), .in1(16'h8000), .out(multiplexer_10_out), .sel(out_16), .en(in_13));
  assign or_3_out = shifter_6_out | multiplexer_10_out;  // OR_Gate or_3, 16 bits wide
  Multiplexer multiplexer_11 (.in0(in_11), .in1(in_12), .out(multiplexer_11_out), .sel(out_16), .en(in_13));
  assign bit_extender_2_out = {{3{1'b0}}, multiplexer_11_out};  // Bit_Extender bit_extender_2
  Adder #(.width(4)) adder_5 (.a(bit_extender_2_out), .b(multiplexer_1_out), .out(adder_5_out));  // open: cin, cout
  BitFinder #(.width(16), .\type ("high1")) bitfinder_1 (.in(or_3_out), .index(bitfinder_1_index));  // open: found
  Shifter #(.width(16)) shifter_7 (.in(or_3_out), .\dist (subtractor_3_out), .out(out_20));
  Subtractor #(.width(4)) subtractor_2 (.a(adder_5_out), .b(subtractor_3_out), .out(out_21));  // open: bin, bout
  Subtractor #(.width(4)) subtractor_3 (.a(4'b1111), .b(bitfinder_1_index), .out(subtractor_3_out));  // open: bin, bout

  // Notes on the sheet:
  //                       Exponents
  //   Exponent diff
  //   Shift right
  //   Control for small exp
endmodule
